# Fritzing sketch RPiSumpPump (saved by Fritzing 0.8.3b)
breadboards: 1

parts:
  LED1 = LED - 5mm [color="Red (633nm)" package="5 mm [THT]"]
  R1 = Resistor [tolerance=±5% resistance=220 package=THT]
  Pi1 = Adafruit Pi Cobbler
  S1 = Pushbutton [package="[THT]"]
  RaspberryPi1 = Raspberry Pi Model B  # not connected

nets:
  N1: LED1.cathode, Pi1.GND
  N2: LED1.anode, R1.Pin_0
  N3: R1.Pin_1, Pi1.#17, S1.Pin_1, S1.Pin_2
  N4: Pi1.3V3, S1.Pin_3, S1.Pin_4

custom parts:
  Adafruit Pi Cobbler: Adafruit Pi Cobbler GPIO Breakout for Raspberry Pi
  Raspberry Pi Model B: Raspberry Pi (Model B)
